# Fritzing sketch Lave (saved by Fritzing 0.9.3b)
breadboards: 1

parts:
  Bauteil1 = Arduino Nano (Rev3.0)
  Bauteil2 = ws2812b [package="smd 2812b"]
  Bauteil3 = ws2812b [package="smd 2812b"]
  12 = ws2812b [package="smd 2812b"]
  Bauteil5 = ws2812b [package="smd 2812b"]
  R1 = Resistor [tolerance=±5% resistance=220 package=THT]

nets:
  VSS: Bauteil1.GND, Bauteil2.VSS, Bauteil3.VSS, 12.VSS, Bauteil5.VSS
  N1: Bauteil1.D8, R1.Pin_0
  VDD: Bauteil1.5V, Bauteil2.VDD, Bauteil3.VDD, 12.VDD, Bauteil5.VDD
  N2: Bauteil2.DOUT, Bauteil5.DIN
  N3: Bauteil2.DIN, Bauteil3.DOUT
  N4: Bauteil3.DIN, R1.Pin_1
  N5: 12.DIN, Bauteil5.DOUT
